// Logisim project cs21_proj.circ as structural Verilog: 8 circuits, main circuit main
module main (
);

  wire CF, CFWrite, CLK, cpu_alu_1_anyflow, cpu_alu_1_nbit, MemAdd, MemWrite, multiplexer_3_out, RegWrite,
       TempWrite;
  wire [1:0] ALUSrcA, ALUSrcB, CFSrc, MemSrc, PCSrc, ResultSrc, TempSrc;
  wire [2:0] Rd, RegSum;
  wire [3:0] ACC, adder_1_out, adder_3_out, ALUOp, ALUOut, bit_extender_1_out, cpu_regfile_1_ra,
       cpu_regfile_1_rb, cpu_regfile_1_re, decode_type_1_instr_type, MemOut, multiplexer_4_out,
       multiplexer_7_out, multiplexer_8_out, RegRead, Result;
  wire [7:0] cpu_regfile_1_rc, multiplexer_5_out;
  wire [11:0] adder_1_out_2;
  wire [15:0] Instr, multiplexer_1_out, multiplexer_2_out, PC_q, Temp;

  Multiplexer #(.select(2), .width(16)) multiplexer_1 (
    .in0({adder_1_out_2, adder_1_out}), .in1({Temp[15:4], adder_1_out}), .out(multiplexer_1_out), .sel(PCSrc));  // open: in2, in3
  Clock cpu_clk (.out(CLK));
  Register #(.width(16)) PC (.D(multiplexer_1_out), .en(1'b1), .clk(CLK), .Q(PC_q));  // open: clr
  Adder #(.width(16)) adder_1 (.a(16'h2), .b(PC_q), .out({adder_1_out_2, adder_1_out}));  // open: cin, cout
  // Probe on ALUOp
  // Probe on ALUSrcA
  // Probe on ALUSrcB
  // Probe on ResultSrc
  // Probe on Rd
  // Probe on MemAdd
  // Probe on MemWrite
  instr_mem instr_mem_1 (.Address(PC_q), .Instr(Instr));
  // Probe on RegWrite
  // Probe on CFWrite
  // Probe on CFSrc
  // Probe on Instr
  // Probe on MemSrc
  // Probe on TempSrc
  Adder #(.width(3)) adder_2 (.a(Instr[3:1]), .b(3'b001), .out(RegSum));  // open: cin, cout
  // Probe on TempWrite
  // Probe on PCSrc
  // Probe on decode_type_1_instr_type
  decode_type decode_type_1 (.instr(Instr), .instr_type(decode_type_1_instr_type));
  Multiplexer #(.select(2), .width(16)) multiplexer_2 (
    .in0({adder_1_out_2, adder_1_out}), .in1({16{1'b0}}), .out(multiplexer_2_out), .sel(TempSrc));  // open: in2, in3
  cpu_ctrl cpu_ctrl_1 (
    .instr(Instr), .instr_type(decode_type_1_instr_type), .ALUOp(ALUOp), .ALUSrcA(ALUSrcA),
    .ALUSrcB(ALUSrcB), .ResultSrc(ResultSrc), .Rd(Rd), .MemAdd(MemAdd), .MemWrite(MemWrite),
    .RegWrite(RegWrite), .CFWrite(CFWrite), .CFSrc(CFSrc), .MemSrc(MemSrc), .TempSrc(TempSrc),
    .TempWrite(TempWrite), .PCSrc(PCSrc));
  Multiplexer #(.select(2)) multiplexer_3 (
    .in0(1'b0), .in1(1'b1), .in2(cpu_alu_1_anyflow), .in3(cpu_alu_1_nbit), .out(multiplexer_3_out),
    .sel(CFSrc));
  cpu_regfile cpu_regfile_1 (
    .WDTemp(multiplexer_2_out), .WD3(Result), .CFD(multiplexer_3_out), .WETemp(TempWrite), .WECF(CFWrite),
    .Reset(1'b0), .CLK(CLK), .WE3(RegWrite), .A1(Rd), .ACC(ACC), .RA(cpu_regfile_1_ra),
    .RB(cpu_regfile_1_rb), .RC(cpu_regfile_1_rc[3:0]), .RD(cpu_regfile_1_rc[7:4]), .RE(cpu_regfile_1_re),
    .CF(CF), .Temp(Temp));
  assign bit_extender_1_out = {{3{1'b0}}, CF};  // Bit_Extender bit_extender_1
  Adder #(.width(4)) adder_3 (.a(ACC), .b(bit_extender_1_out), .out(adder_3_out));  // open: cin, cout
  Multiplexer #(.select(2), .width(4)) multiplexer_4 (
    .in0(ACC), .in1(MemOut), .in2(adder_3_out), .in3(RegRead), .out(multiplexer_4_out), .sel(ALUSrcA));
  Multiplexer #(.width(8)) multiplexer_5 (
    .in0({cpu_regfile_1_rb, cpu_regfile_1_ra}), .in1(cpu_regfile_1_rc), .out(multiplexer_5_out), .sel(MemAdd));
  Multiplexer #(.select(3), .width(4)) multiplexer_6 (
    .in0(ACC), .in1(cpu_regfile_1_ra), .in2(cpu_regfile_1_rb), .in3(cpu_regfile_1_rc[3:0]),
    .in4(cpu_regfile_1_rc[7:4]), .in5(cpu_regfile_1_re), .out(RegRead), .sel(RegSum));  // open: in6, in7
  Multiplexer #(.select(2), .width(4)) multiplexer_7 (
    .in0(MemOut), .in3(4'b0001), .out(multiplexer_7_out), .sel(ALUSrcB));  // open: in1, in2
  Multiplexer #(.select(2), .width(4)) multiplexer_8 (
    .in0(ALUOut), .in1(ACC), .out(multiplexer_8_out), .sel(MemSrc));  // open: in2, in3
  cpu_alu cpu_alu_1 (
    .arg1(multiplexer_4_out), .arg2(multiplexer_7_out), .CF(CF), .ALUOp(ALUOp), .anyflow(cpu_alu_1_anyflow),
    .q(ALUOut), .NBit(cpu_alu_1_nbit));
  RAM #(.asyncread("true"), .dataWidth(4)) ram_1 (
    .addr(multiplexer_5_out), .we(MemWrite), .oe(1'b1), .clk(CLK), .din(multiplexer_8_out), .dout(MemOut));
  Multiplexer #(.select(2), .width(4)) multiplexer_9 (
    .in0(ALUOut), .in1(MemOut), .in2(RegRead), .out(Result), .sel(ResultSrc));  // open: in3
endmodule

module range_compare (
  input  [2:0] val,
  input  [2:0] lt,
  input  [2:0] gt,
  output q
);

  wire comparator_1_eq, comparator_1_lt, comparator_2_eq, comparator_2_gt, or_1_out, or_2_out;

  Comparator #(.mode("unsigned"), .width(3)) comparator_1 (
    .a(val), .b(lt), .eq(comparator_1_eq), .lt(comparator_1_lt));  // open: gt
  Comparator #(.mode("unsigned"), .width(3)) comparator_2 (
    .a(val), .b(gt), .gt(comparator_2_gt), .eq(comparator_2_eq));  // open: lt
  or or_1 (or_1_out, comparator_1_eq, comparator_1_lt);
  or or_2 (or_2_out, comparator_2_gt, comparator_2_eq);
  and and_1 (q, or_1_out, or_2_out);
endmodule

module decode_type (
  input  [15:0] instr,
  output [3:0] instr_type
);

  wire and_1_out, and_2_out, and_3_out, and_4_out, and_5_out, and_6_out, and_7_out, and_8_out,
       comparator_3_eq, comparator_4_eq, comparator_5_eq, comparator_6_eq, comparator_7_eq, comparator_8_eq,
       FourToSeven, or_1_out, or_2_out, range_compare_4_q, range_compare_6_q, SixToSix, TwoToSeven,
       ZeroToThree;

  Comparator #(.width(5)) comparator_1 (.a(instr[7:3]), .b(5'b00111));  // open: gt, eq, lt
  Comparator #(.width(5)) comparator_2 (.a(instr[7:3]), .b(5'b00110));  // open: gt, eq, lt
  Comparator #(.width(5)) comparator_3 (.a(instr[7:3]), .b(5'b00101), .eq(comparator_3_eq));  // open: gt, lt
  Comparator #(.width(5)) comparator_4 (.a(instr[7:3]), .b(5'b00100), .eq(comparator_4_eq));  // open: gt, lt
  Comparator #(.width(5)) comparator_5 (.a(instr[7:3]), .b(5'b00011), .eq(comparator_5_eq));  // open: gt, lt
  Comparator #(.width(5)) comparator_6 (.a(instr[7:3]), .b(5'b00010), .eq(comparator_6_eq));  // open: gt, lt
  Comparator #(.width(5)) comparator_7 (.a(instr[7:3]), .b(5'b00001), .eq(comparator_7_eq));  // open: gt, lt
  Comparator #(.width(5)) comparator_8 (.a(instr[7:3]), .b({5{1'b0}}), .eq(comparator_8_eq));  // open: gt, lt
  // Probe on instr[2:0]
  range_compare range_compare_1 (.val(instr[2:0]), .lt(3'b011), .gt(3'b000), .q(ZeroToThree));
  range_compare range_compare_2 (.val(instr[2:0]), .lt(3'b111), .gt(3'b100), .q(FourToSeven));
  range_compare range_compare_3 (.val(instr[2:0]), .lt(3'b111), .gt(3'b010), .q(TwoToSeven));
  range_compare range_compare_4 (.val(instr[2:0]), .lt(3'b011), .gt(3'b010), .q(range_compare_4_q));
  range_compare range_compare_5 (.val(instr[2:0]), .lt(3'b110), .gt(3'b110), .q(SixToSix));
  range_compare range_compare_6 (.val(instr[3:1]), .lt(3'b100), .gt(3'b000), .q(range_compare_6_q));
  and and_1 (and_1_out, ZeroToThree, comparator_8_eq);
  and and_2 (and_2_out, FourToSeven, comparator_8_eq);
  and and_3 (and_3_out, comparator_7_eq, ZeroToThree);
  and and_4 (and_4_out, comparator_7_eq, FourToSeven);
  buf and_5 (and_5_out, TwoToSeven);  // AND_Gate
  and and_6 (and_6_out, range_compare_4_q, comparator_3_eq);
  and and_7 (and_7_out, SixToSix, comparator_3_eq);
  or or_1 (or_1_out, comparator_6_eq, comparator_5_eq);
  or or_2 (or_2_out, comparator_4_eq, comparator_3_eq);
  and and_8 (and_8_out, or_1_out, range_compare_6_q);
  Priority_Encoder #(.select(4)) priority_encoder_1 (
    .in0(and_1_out), .in1(and_2_out), .in2(and_3_out), .in3(and_4_out), .in4(and_5_out), .in5(and_6_out),
    .in6(and_7_out), .in7(and_8_out), .in8(or_2_out), .out(instr_type));  // open: in9, in10, in11, in12, in13, in14, in15, gs, en_out, en_in

  // Other names for the same wires on the sheet: Func3Reg[2:0] = instr[3:1]; BitOne = instr[0]

  // Notes on the sheet:
  //   opcode: 00101, func3: 110
  //   opcode: 00000, func3: 000 - 011
  //   opcode: 00000, func3: 100 - 111
  //   opcode: 00001, func3: 000 - 011
  //   opcode: 00001, func3: 000 - 011
  //   opcode: 00011, func3: 010 - 111
  //   opcode: 00101, func3: 010 - 011
  //   opcode: 0010(000 - 100)X, func3: X
  //   opcode: 0001(000 - 100)X, func3: X
endmodule

module cpu_ctrl (
  input  [15:0] instr,
  input  [3:0] instr_type,
  output [3:0] ALUOp,
  output [1:0] ALUSrcA,
  output [1:0] ALUSrcB,
  output [1:0] ResultSrc,
  output [2:0] Rd,
  output MemAdd,
  output MemWrite,
  output RegWrite,
  output CFWrite,
  output [1:0] CFSrc,
  output [1:0] MemSrc,
  output [1:0] TempSrc,
  output TempWrite,
  output [1:0] PCSrc
);

  wire comparator_1_eq, comparator_2_eq, comparator_3_eq, comparator_4_eq, comparator_5_eq, comparator_6_eq,
       multiplexer_2_out, multiplexer_4_out, multiplexer_5_out, not_1_out, not_2_out, or_1_out, or_2_out,
       or_3_out, or_4_out;
  wire [1:0] bit_extender_1_out, multiplexer_9_out, priority_encoder_1_out;
  wire [2:0] adder_1_out, adder_2_out, multiplexer_7_out;
  wire [3:0] multiplexer_1_out, multiplexer_3_out, multiplexer_6_out, multiplexer_8_out, multiplexer_10_out;
  wire [25:0] decode_joiner_1_opcodes, decode_joiner_2_opcodes, decode_joiner_3_opcodes,
       decode_joiner_4_opcodes, decode_joiner_5_opcodes, decode_joiner_6_opcodes, decode_joiner_7_opcodes,
       decode_joiner_8_opcodes, decode_joiner_9_opcodes;

  Adder #(.width(3)) adder_1 (.a(instr[3:1]), .b(3'b001), .out(adder_1_out));  // open: cin, cout
  Comparator #(.mode("unsigned"), .width(3)) comparator_1 (
    .a(instr[2:0]), .b(3'b010), .eq(comparator_1_eq));  // open: gt, lt
  Comparator #(.mode("unsigned"), .width(3)) comparator_2 (
    .a(instr[2:0]), .b(3'b101), .eq(comparator_2_eq));  // open: gt, lt
  Comparator #(.mode("unsigned"), .width(3)) comparator_3 (
    .a(instr[2:0]), .b(3'b011), .eq(comparator_3_eq));  // open: gt, lt
  Comparator #(.mode("unsigned"), .width(3)) comparator_4 (
    .a(instr[2:0]), .b(3'b110), .eq(comparator_4_eq));  // open: gt, lt
  Comparator #(.mode("unsigned"), .width(3)) comparator_5 (
    .a(instr[2:0]), .b(3'b100), .eq(comparator_5_eq));  // open: gt, lt
  Comparator #(.mode("unsigned"), .width(3)) comparator_6 (
    .a(instr[2:0]), .b(3'b111), .eq(comparator_6_eq));  // open: gt, lt
  Multiplexer #(.width(4)) multiplexer_1 (.in0(4'b0010), .in1(4'b0011), .out(multiplexer_1_out), .sel(instr[0]));
  Multiplexer multiplexer_2 (.in0(1'b0), .in1(1'b1), .out(multiplexer_2_out), .sel(instr[1]));
  Multiplexer #(.width(4)) multiplexer_3 (.in0(4'b0010), .in1(4'b0011), .out(multiplexer_3_out), .sel(instr[1]));
  Multiplexer multiplexer_4 (.in0(1'b0), .in1(1'b1), .out(multiplexer_4_out), .sel(instr[1]));
  Multiplexer multiplexer_5 (.in0(1'b0), .in1(1'b1), .out(multiplexer_5_out), .sel(instr[0]));
  Multiplexer #(.select(2), .width(4)) multiplexer_6 (
    .in0(4'b0000), .in1(4'b0001), .in2(4'b0111), .in3(4'b1000), .out(multiplexer_6_out), .sel(instr[1:0]));
  Multiplexer #(.width(3)) multiplexer_7 (.in0(adder_1_out), .in1(3'b000), .out(multiplexer_7_out), .sel(instr[0]));
  Multiplexer #(.width(4)) multiplexer_8 (.in0(4'b0010), .in1(4'b0011), .out(multiplexer_8_out), .sel(instr[0]));
  assign bit_extender_1_out = {{1{1'b0}}, instr[0]};  // Bit_Extender bit_extender_1
  or or_1 (or_1_out, comparator_1_eq, comparator_2_eq);
  or or_2 (or_2_out, comparator_3_eq, comparator_4_eq);
  or or_3 (or_3_out, comparator_5_eq, comparator_6_eq);
  Multiplexer #(.width(2)) multiplexer_9 (.in0(2'b10), .in1(2'b00), .out(multiplexer_9_out), .sel(instr[0]));
  Adder #(.width(3)) adder_2 (.a(instr[3:1]), .b(3'b001), .out(adder_2_out));  // open: cin, cout
  Priority_Encoder #(.select(2)) priority_encoder_1 (
    .in0(or_1_out), .in1(or_2_out), .in2(or_3_out), .out(priority_encoder_1_out));  // open: in3, gs, en_out, en_in
  or or_4 (or_4_out, comparator_1_eq, comparator_3_eq, comparator_5_eq);
  Multiplexer #(.select(2), .width(4)) multiplexer_10 (
    .in0(4'b0100), .in1(4'b0101), .in2(4'b0110), .out(multiplexer_10_out), .sel(priority_encoder_1_out));  // open: in3
  not not_1 (not_1_out, multiplexer_5_out);
  not not_2 (not_2_out, or_4_out);
  decode_joiner decode_joiner_1 (
    .ALUOp(4'b0000), .ALUSrcA(2'b00), .ALUSrcB(2'b00), .ResultSrc(2'b10), .Rd(multiplexer_7_out),
    .MemAdd(1'b0), .MemWrite(1'b0), .RegWrite(1'b1), .CFWrite(1'b0), .TempWrite(1'b0), .PCSrc(2'b00),
    .opcodes(decode_joiner_1_opcodes));  // open: CFSrc, MemSrc, TempSrc
  decode_joiner decode_joiner_2 (
    .ALUOp(multiplexer_8_out), .ALUSrcA(2'b11), .ALUSrcB(2'b11), .ResultSrc(2'b00), .Rd(adder_2_out),
    .MemWrite(1'b0), .RegWrite(1'b1), .CFWrite(1'b0), .CFSrc(2'b00), .TempWrite(1'b0), .PCSrc(2'b00),
    .opcodes(decode_joiner_2_opcodes));  // open: MemAdd, MemSrc, TempSrc
  decode_joiner decode_joiner_3 (
    .ALUOp(4'b0000), .ALUSrcA(2'b00), .ALUSrcB(2'b00), .ResultSrc(2'b00), .Rd(3'b000), .MemAdd(1'b0),
    .MemWrite(1'b0), .RegWrite(1'b0), .CFWrite(1'b0), .CFSrc(2'b00), .MemSrc(2'b00), .TempSrc(2'b01),
    .TempWrite(1'b0), .PCSrc(2'b01), .opcodes(decode_joiner_3_opcodes));
  decode_joiner decode_joiner_4 (
    .ALUOp(4'b0000), .ALUSrcA(2'b00), .ALUSrcB(2'b00), .ResultSrc(2'b00), .Rd(3'b000), .MemAdd(1'b0),
    .MemWrite(1'b0), .RegWrite(1'b0), .CFWrite(1'b1), .CFSrc(bit_extender_1_out), .MemSrc(2'b00),
    .TempSrc(2'b00), .TempWrite(1'b0), .PCSrc(2'b00), .opcodes(decode_joiner_4_opcodes));
  decode_joiner decode_joiner_5 (
    .ALUOp(multiplexer_1_out), .ALUSrcA(2'b01), .ALUSrcB(2'b11), .ResultSrc(2'b00), .Rd(3'b000),
    .MemAdd(multiplexer_2_out), .MemWrite(1'b1), .RegWrite(1'b0), .CFWrite(1'b0), .CFSrc(2'b00),
    .MemSrc(2'b01), .TempSrc(2'b00), .TempWrite(1'b0), .PCSrc(2'b00), .opcodes(decode_joiner_5_opcodes));
  decode_joiner decode_joiner_6 (
    .ALUOp(multiplexer_3_out), .ALUSrcA(multiplexer_9_out), .ALUSrcB(2'b00), .ResultSrc(2'b00), .Rd(3'b000),
    .MemAdd(1'b0), .MemWrite(1'b0), .RegWrite(1'b1), .CFWrite(1'b1), .CFSrc(2'b10), .MemSrc(2'b00),
    .TempSrc(2'b00), .TempWrite(1'b0), .PCSrc(2'b00), .opcodes(decode_joiner_6_opcodes));
  decode_joiner decode_joiner_7 (
    .ALUOp(multiplexer_6_out), .ALUSrcA(2'b00), .ALUSrcB(2'b00), .ResultSrc(2'b00), .Rd(3'b000),
    .MemAdd(1'b0), .MemWrite(1'b0), .RegWrite(1'b1), .CFWrite(instr[1]), .CFSrc(2'b11), .MemSrc(2'b00),
    .TempSrc(2'b00), .TempWrite(1'b0), .PCSrc(2'b00), .opcodes(decode_joiner_7_opcodes));
  decode_joiner decode_joiner_8 (
    .ALUOp(4'b0000), .ALUSrcA(2'b00), .ALUSrcB(2'b00), .ResultSrc(2'b01), .Rd(3'b000),
    .MemAdd(multiplexer_4_out), .MemWrite(multiplexer_5_out), .RegWrite(not_1_out), .CFWrite(1'b0),
    .CFSrc(2'b00), .MemSrc(2'b01), .TempSrc(2'b00), .TempWrite(1'b0), .PCSrc(2'b00),
    .opcodes(decode_joiner_8_opcodes));
  decode_joiner decode_joiner_9 (
    .ALUOp(multiplexer_10_out), .ALUSrcA(2'b00), .ALUSrcB(2'b00), .ResultSrc(2'b00), .Rd(3'b000),
    .MemAdd(1'b0), .MemWrite(not_2_out), .RegWrite(or_4_out), .CFWrite(1'b0), .CFSrc(2'b00), .MemSrc(2'b00),
    .TempSrc(2'b00), .TempWrite(1'b0), .PCSrc(2'b00), .opcodes(decode_joiner_9_opcodes));
  Multiplexer #(.select(4), .width(26)) multiplexer_11 (
    .in0(decode_joiner_7_opcodes), .in1(decode_joiner_8_opcodes), .in2(decode_joiner_6_opcodes),
    .in3(decode_joiner_5_opcodes), .in4(decode_joiner_9_opcodes), .in5(decode_joiner_4_opcodes),
    .in6(decode_joiner_3_opcodes), .in7(decode_joiner_2_opcodes), .in8(decode_joiner_1_opcodes),
    .out({PCSrc, TempWrite, TempSrc, MemSrc, CFSrc, CFWrite, RegWrite, MemWrite, MemAdd, Rd, ResultSrc, ALUSrcB, ALUSrcA, ALUOp}),
    .sel(instr_type));  // open: in9, in10, in11, in12, in13, in14, in15
  // Probe on instr_type

  // Other names for the same wires on the sheet: RegSum[2:0] = instr[3:1]

  // Notes on the sheet:
  //   ALUOp
  //   Type B (ACC to / from Mem)
  //   MemAdd
  //   MemWrite
  //   ALU Operation
  //   Type A (Rotation)
  //   RegWrite
endmodule

module decode_joiner (
  input  [3:0] ALUOp,
  input  [1:0] ALUSrcA,
  input  [1:0] ALUSrcB,
  input  [1:0] ResultSrc,
  input  [2:0] Rd,
  input  MemAdd,
  input  MemWrite,
  input  RegWrite,
  input  CFWrite,
  input  [1:0] CFSrc,
  input  [1:0] MemSrc,
  input  [1:0] TempSrc,
  input  TempWrite,
  input  [1:0] PCSrc,
  output [25:0] opcodes
);


  assign opcodes = {PCSrc, TempWrite, TempSrc, MemSrc, CFSrc, CFWrite, RegWrite, MemWrite, MemAdd, Rd, ResultSrc, ALUSrcB, ALUSrcA, ALUOp};
endmodule

module cpu_regfile (
  input  [15:0] WDTemp,
  input  [3:0] WD3,
  input  CFD,
  input  WETemp,
  input  WECF,
  input  Reset,
  input  CLK,
  input  WE3,
  input  [2:0] A1,
  output [3:0] ACC,
  output [3:0] RA,
  output [3:0] RB,
  output [3:0] RC,
  output [3:0] RD,
  output [3:0] RE,
  output CF,
  output [15:0] Temp
);

  wire w0, w1, w2, w3, w4, w5, WETemp_t, wr0, wr1, wr2, wr3, wr4, wr5;

  Register #(.width(4)) register_1 (.D(WD3), .en(w0), .clk(CLK), .Q(ACC), .clr(Reset));
  Register #(.width(4)) register_2 (.D(WD3), .en(w1), .clk(CLK), .Q(RA), .clr(Reset));
  Register #(.width(4)) register_3 (.D(WD3), .en(w2), .clk(CLK), .Q(RB), .clr(Reset));
  Register #(.width(4)) register_4 (.D(WD3), .en(w3), .clk(CLK), .Q(RC), .clr(Reset));
  Register #(.width(4)) register_5 (.D(WD3), .en(w4), .clk(CLK), .Q(RD), .clr(Reset));
  Register #(.width(4)) register_6 (.D(WD3), .en(w5), .clk(CLK), .Q(RE), .clr(Reset));
  Register #(.width(1)) register_7 (.D(CFD), .en(WECF), .clk(CLK), .Q(CF), .clr(Reset));
  Register #(.width(16)) register_8 (.D(WDTemp), .en(WETemp_t), .clk(CLK), .Q(Temp), .clr(Reset));
  Decoder #(.select(3)) decoder_1 (
    .out0(wr0), .out1(wr1), .out2(wr2), .out3(wr3), .out4(wr4), .out5(wr5), .sel(A1));  // open: out6, out7, en
  and and_1 (w0, wr0, WE3);
  and and_2 (w1, wr1, WE3);
  and and_3 (w2, wr2, WE3);
  and and_4 (w3, wr3, WE3);
  and and_5 (w4, wr4, WE3);
  and and_6 (w5, wr5, WE3);

  // Other names for the same wires on the sheet: o0[3:0] = ACC
endmodule

module cpu_alu (
  input  [3:0] arg1,
  input  [3:0] arg2,
  input  CF,
  input  [3:0] ALUOp,
  output anyflow,
  output [3:0] q,
  output NBit
);

  wire adder_1_cout, subtractor_1_bout;
  wire [3:0] adder_1_out, and_1_out, or_1_out, subtractor_1_out, xor_1_out;

  assign and_1_out = arg1 & arg2;  // AND_Gate and_1, 4 bits wide
  assign or_1_out = arg1 | arg2;  // OR_Gate or_1, 4 bits wide
  assign xor_1_out = arg1 ^ arg2;  // XOR_Gate xor_1, 4 bits wide
  Adder #(.width(4)) adder_1 (.a(arg1), .b(arg2), .out(adder_1_out), .cout(adder_1_cout));  // open: cin
  Subtractor #(.width(4)) subtractor_1 (
    .a(arg1), .b(arg2), .out(subtractor_1_out), .bout(subtractor_1_bout));  // open: bin
  or or_2 (anyflow, adder_1_cout, subtractor_1_bout);
  Multiplexer #(.select(4)) multiplexer_1 (
    .in0(1'b0), .in1(1'b0), .in2(1'b0), .in3(1'b0), .in4(1'b0), .in5(1'b0), .in6(1'b0), .in7(arg1[0]),
    .in8(arg1[3]), .in9(1'b0), .in10(1'b0), .in11(1'b0), .in12(1'b0), .in13(1'b0), .in14(1'b0), .in15(1'b0),
    .out(NBit), .sel(ALUOp));
  Multiplexer #(.select(4), .width(4)) multiplexer_2 (
    .in0({arg1[0], arg1[3:1]}), .in1({arg1[2:0], arg1[3]}), .in2(adder_1_out), .in3(subtractor_1_out),
    .in4(and_1_out), .in5(or_1_out), .in6(xor_1_out), .in7({CF, arg1[3:1]}), .in8({arg1[2:0], CF}),
    .in9(4'b0000), .in10(4'b0000), .in11(4'b0000), .in12(4'b0000), .in13(4'b0000), .in14(4'b0000),
    .in15(4'b0000), .out(q), .sel(ALUOp));
endmodule

module instr_mem (
  input  [15:0] Address,
  output [15:0] Instr
);

  ROM #(.addrWidth(15), .dataWidth(16)) rom_1 (.addr(Address[15:1]), .data(Instr));

  // Notes on the sheet:
  //   // Nasty hack to make word-addressable ROM usable
  //   contents of rom_1 (hex, n*v repeats v):
  //   28 1 2 3
endmodule
